# Fritzing sketch embedded_light_flow_system (saved by Fritzing 1.0.4)
breadboards: 1

parts:
  Part1 = Arduino Uno (Rev3) - ICSP
  J1 = Basic Servo
  R1 = Photocell (LDR) [power=0.25W dark_resistance_@0.01lx=300kΩ light_resistance_@100lx=400Ω luminance=10lx package=THT]
  R2 = Resistor [tolerance=±5% resistance=220 package="2512 [SMD]"]
  R3 = Resistor [tolerance=±5% resistance=220 package="2512 [SMD]"]
  R4 = Resistor [tolerance=±5% resistance=220 package="2512 [SMD]"]
  R5 = Resistor [tolerance=±5% resistance=220 package="2512 [SMD]"]
  LED1 = LED - 5mm [color="Blue (525nm)" current=0.030A package="5 mm [THT]"]
  LED2 = LED - 5mm [color="Red (633nm)" current=0.030A package="5 mm [THT]"]
  LED3 = LED - 5mm [color="Yellow (595nm)" current=0.030A package="5 mm [THT]"]
  S1 = Pushbutton [package="[THT]"]  # not connected
  R6 = Resistor [tolerance=±5% resistance=10k package="2512 [SMD]"]

nets:
  N1: Part1.A0, R1.pin_1, R2.Pin_0
  N2: Part1.D10_PWM/SS, R3.Pin_1
  N3: Part1.D11_PWM/MOSI, R4.Pin_1
  N4: Part1.D12/MISO, R5.Pin_1
  N5: Part1.D13/SCK, J1.pulse
  N6: Part1.D2, R6.Pin_0
  5V: Part1.5V, J1.vcc, R1.pin_0
  GND: Part1.GND, J1.gnd, R2.Pin_1, LED1.cathode, LED2.cathode, LED3.cathode, R6.Pin_1
  N7: R4.Pin_0, LED2.anode
  N8: R5.Pin_0, LED1.anode
